// Logisim project Processor.circ as structural Verilog: 8 circuits, main circuit Processor
module Processor (
  input  Reset,
  input  [3:0] Display_Address
);

  wire alu_1_is, alu_1_is_2, branch_unit_1_isbranchtaken, Clock, control_unit_1_isimmediate, flags_1_flags_e,
       flags_1_flags_gt;
  wire [2:0] L44O;
  wire [3:0] L34O, multiplexer_5_out, multiplexer_6_out, multiplexer_7_out, register_file_1_displayd_2,
       register_file_1_displayd_3;
  wire [7:0] L26I, L26O;
  wire [12:0] control_unit_1_alusignals;
  wire [23:0] register_file_1_displayd;
  wire [31:0] adder_1_out, adder_2_out, bit_extender_1_out, calculate_immediate_1_immx, L10I, L10O, L11I,
       L11O, L20O, L21I, L21O, L22I, L22O, L23I, L23O, L24I, L24O, L25O, L30O, L31I, L31O, L32O, L33O, L40O,
       L41O, L42I, L42O, L43O, multiplexer_1_out, multiplexer_2_out, multiplexer_3_out, shifter_1_out;

  Register #(.width(32), .trigger("falling")) PC (
    .D(multiplexer_1_out), .Q(L10I), .clk(Clock), .clr(Reset));  // open: en
  Multiplexer #(.width(32), .enable("false")) multiplexer_1 (
    .in0(adder_1_out), .in1(multiplexer_2_out), .out(multiplexer_1_out), .sel(branch_unit_1_isbranchtaken));
  assign bit_extender_1_out = {{5{L11O[26]}}, L11O[26:0]};  // Bit_Extender bit_extender_1
  Adder #(.width(32)) adder_1 (.a(32'h4), .b(L10I), .out(adder_1_out));  // open: cin, cout
  Shifter #(.width(32)) shifter_1 (.in(bit_extender_1_out), .\dist (5'b00010), .out(shifter_1_out));
  ALU alu_1 (
    .A(L22O), .B(L23O), .ALUsignals(control_unit_1_alusignals), .aluResult(L31I), .is(alu_1_is),
    .is_2(alu_1_is_2));
  Adder #(.width(32)) adder_2 (.a(L40O), .b(32'h4), .out(adder_2_out));  // open: cin, cout
  Calculate_Immediate calculate_immediate_1 (.imm(L11O[17:0]), .immx(calculate_immediate_1_immx));
  Adder #(.width(32)) adder_3 (.a(shifter_1_out), .b(L10O), .out(L21I));  // open: cin, cout
  Multiplexer #(.width(32), .enable("false")) multiplexer_2 (
    .in0(L21O), .in1(L22O), .out(multiplexer_2_out), .sel(L26O[6]));
  Multiplexer #(.select(2), .width(32), .enable("false")) multiplexer_3 (
    .in0(L41O), .in1(L42O), .in2(adder_2_out), .out(multiplexer_3_out), .sel({L44O[0], L44O[1]}));  // open: in3
  Clock u_Clock (.out(Clock));
  ROM #(.addrWidth(24), .dataWidth(32)) rom_1 (.addr(L10I[25:2]), .data(L11I));  // open: sel
  Multiplexer #(.width(32), .enable("false")) multiplexer_4 (
    .in0(L24I), .in1(calculate_immediate_1_immx), .out(L23I), .sel(control_unit_1_isimmediate));
  Flags flags_1 (
    .isCmp(control_unit_1_alusignals[0]), .is(alu_1_is), .is_2(alu_1_is_2), .flags_GT(flags_1_flags_gt),
    .flags_E(flags_1_flags_e));
  Memory_Unit memory_unit_1 (
    .MAR(L31O), .ldResult(L42I), .MDR(L32O), .isSt(L34O[1]), .isLd(L34O[2]), .Clock(Clock), .Reset(Reset));
  Hex_Digit_Display hex_digit_display_1 (.value(register_file_1_displayd_3));  // open: dp
  Multiplexer #(.width(4), .enable("false")) multiplexer_5 (
    .in0(L11O[17:14]), .in1(L11O[25:22]), .out(multiplexer_5_out), .sel(L26I[4]));
  Hex_Digit_Display hex_digit_display_2 (.value(register_file_1_displayd_2));  // open: dp
  Multiplexer #(.width(4), .enable("false")) multiplexer_6 (
    .in0(L11O[21:18]), .in1(4'b1111), .out(multiplexer_6_out), .sel(L26I[6]));
  Register_File register_file_1 (
    .ReadA1(multiplexer_6_out), .ReadA2(multiplexer_5_out), .WriteE(L44O[2]), .WriteD(multiplexer_3_out),
    .ReadD1(L22I), .ReadD2(L24I), .Clock(Clock), .Reset(Reset),
    .DisplayD({register_file_1_displayd_3, register_file_1_displayd_2, register_file_1_displayd}),
    .DisplayA(Display_Address), .WriteA(multiplexer_7_out));
  Hex_Digit_Display hex_digit_display_3 (.value(register_file_1_displayd[23:20]));  // open: dp
  Branch_Unit branch_unit_1 (
    .isBeq(L26O[2]), .isUBranch(L26O[0]), .flags_E(flags_1_flags_e), .isBgt(L26O[1]),
    .flags_GT(flags_1_flags_gt), .isBranchTaken(branch_unit_1_isbranchtaken));
  Hex_Digit_Display hex_digit_display_4 (.value(register_file_1_displayd[15:12]));  // open: dp
  Hex_Digit_Display hex_digit_display_5 (.value(register_file_1_displayd[19:16]));  // open: dp
  Control_Unit control_unit_1 (
    .isSt(L26I[4]), .isLd(L26I[5]), .isBeq(L26I[2]), .isBgt(L26I[1]), .isRet(L26I[6]), .I_bit(L11O[26]),
    .isImmediate(control_unit_1_isimmediate), .opcode(L11O[31:27]), .isWb(L26I[7]), .isUbranch(L26I[0]),
    .isCall(L26I[3]), .ALUsignals(control_unit_1_alusignals));
  Hex_Digit_Display hex_digit_display_6 (.value(register_file_1_displayd[11:8]));  // open: dp
  Hex_Digit_Display hex_digit_display_7 (.value(register_file_1_displayd[7:4]));  // open: dp
  Multiplexer #(.width(4), .enable("false")) multiplexer_7 (
    .in0(L43O[25:22]), .in1(4'b1111), .out(multiplexer_7_out), .sel(L26I[3]));
  Hex_Digit_Display hex_digit_display_8 (.value(register_file_1_displayd[3:0]));  // open: dp
  // Probe on {register_file_1_displayd_3, register_file_1_displayd_2, register_file_1_displayd}
  Register #(.width(32), .trigger("low")) register_1 (.D(L20O), .Q(L30O), .clk(Clock), .clr(Reset));  // open: en
  Register #(.width(32), .trigger("low")) register_2 (.D(L31I), .Q(L31O), .clk(Clock), .clr(Reset));  // open: en
  Register #(.width(32), .trigger("low")) register_3 (.D(L24O), .Q(L32O), .clk(Clock), .clr(Reset));  // open: en
  Register #(.width(4), .trigger("low")) register_4 (
    .D({L26O[7], L26O[5:3]}), .Q(L34O), .clk(Clock), .clr(Reset));  // open: en
  Register #(.width(32), .trigger("low")) register_5 (.D(L30O), .Q(L40O), .clk(Clock), .clr(Reset));  // open: en
  Register #(.width(32), .trigger("low")) register_6 (.D(L31O), .Q(L41O), .clk(Clock), .clr(Reset));  // open: en
  Register #(.width(32), .trigger("low")) register_7 (.D(L42I), .Q(L42O), .clk(Clock), .clr(Reset));  // open: en
  Register #(.width(32), .trigger("low")) register_8 (.D(L33O), .Q(L43O), .clk(Clock), .clr(Reset));  // open: en
  Register #(.width(3), .trigger("low")) register_9 (
    .D({L34O[3:2], L34O[0]}), .Q(L44O), .clk(Clock), .clr(Reset));  // open: en
  Register #(.width(32), .trigger("low")) register_10 (.D(L11I), .Q(L11O), .clk(Clock), .clr(Reset));  // open: en
  Register #(.width(32), .trigger("low")) register_11 (.D(L10I), .Q(L10O), .clk(Clock), .clr(Reset));  // open: en
  Register #(.width(32), .trigger("low")) register_12 (.D(L10O), .Q(L20O), .clk(Clock), .clr(Reset));  // open: en
  Register #(.width(32), .trigger("low")) register_13 (.D(L21I), .Q(L21O), .clk(Clock), .clr(Reset));  // open: en
  Register #(.width(32), .trigger("low")) register_14 (.D(L22I), .Q(L22O), .clk(Clock), .clr(Reset));  // open: en
  Register #(.width(32), .trigger("low")) register_15 (.D(L23I), .Q(L23O), .clk(Clock), .clr(Reset));  // open: en
  Register #(.width(32), .trigger("low")) register_16 (.D(L24I), .Q(L24O), .clk(Clock), .clr(Reset));  // open: en
  Register #(.width(32), .trigger("low")) register_17 (.D(L11O), .Q(L25O), .clk(Clock), .clr(Reset));  // open: en
  Register #(.trigger("low")) register_18 (.D(L26I), .Q(L26O), .clk(Clock), .clr(Reset));  // open: en

  // Other names for the same wires on the sheet: L20I[31:0] = L10O; L25I[31:0] = L11O; L30I[31:0] = L20O;
  //   L32I[31:0] = L24O; L33I[31:0] = L25O; L34I[3:0] = {L26O[7], L26O[5:3]}; L40I[31:0] = L30O; L41I[31:0] = L31O;
  //   L43I[31:0] = L33O; L44I[2:0] = {L34O[3:2], L34O[0]}; Wb = L44O[2]

  // Notes on the sheet:
  //   isBranchTaken
  //   ALUsignals
  //   pc
  //   pc+4
  //   branchTarget
  //   offset
  //   pc
  //   B
  //   ALU
  //   aluResult
  //   MAR
  //   ldResult
  //   Instruction Memory
  //   calc immx
  //   imm
  //   branchTarget
  //   isBranchTaken
  //   A
  //   is>
  //   is=
  //   MDR
  //   Memory
  //   Unit
  //   data
  //   SINGLE CYCLE PROCESSOR
  //   contents of rom_1 (hex, n*v repeats v):
  //   4c400010 4c800018 c48000 90000000
  //   immx
  //   isRet
  //   Flags
  //   isCmp
  //   isLd
  //   isSt
  //   isLd
  //   isCall
  //   instruction
  //   rs2
  //   rd
  //   isSt
  //   op2
  //   isImmediate
  //   flags(GT)
  //   flags(E)
  //   rs1
  //   E
  //   Register
  //   A
  //   File
  //   D
  //   op1
  //   Branch
  //   Unit
  //   isRet
  //   isWb
  //   address
  //   data
  //   isBeq
  //   isBgt
  //   isUBranch
  //   Display Register
  //   opcode
  //   CONTROL
  //   I bit
  //   UNIT
  //   isCall
  //   rd
  //   EX-MA LATCH
  //   MA-RW LATCH
  //   IF-OF LATCH
  //   OF-EX LATCH
endmodule

module Control_Unit (
  input  I_bit,
  input  [4:0] opcode,
  output isSt,
  output isLd,
  output isBeq,
  output isBgt,
  output isRet,
  output isImmediate,
  output isWb,
  output isUbranch,
  output isCall,
  output [12:0] ALUsignals
);

  wire and_6_out, and_7_out, and_8_out, and_9_out, and_10_out, and_12_out, and_13_out, nand_1_out;

  nand nand_1 (nand_1_out, opcode[0], opcode[1]);
  and and_1 (isSt, opcode[0], opcode[1], opcode[2], opcode[3], ~opcode[4]);  // AND_Gate
  and and_2 (isLd, ~opcode[0], opcode[1], opcode[2], opcode[3], ~opcode[4]);  // AND_Gate
  and and_3 (isBeq, ~opcode[0], ~opcode[1], ~opcode[2], ~opcode[3], opcode[4]);  // AND_Gate
  and and_4 (isBgt, opcode[0], ~opcode[1], ~opcode[2], ~opcode[3], opcode[4]);  // AND_Gate
  and and_5 (isRet, ~opcode[0], ~opcode[1], opcode[2], ~opcode[3], opcode[4]);  // AND_Gate
  and and_6 (and_6_out, opcode[0], ~opcode[1], opcode[2], ~opcode[4]);  // AND_Gate
  and and_7 (and_7_out, opcode[0], opcode[2], opcode[3], ~opcode[4]);  // AND_Gate
  and and_8 (and_8_out, opcode[4], nand_1_out);
  and and_9 (and_9_out, opcode[1], ~opcode[2], ~opcode[3], opcode[4]);  // AND_Gate
  and and_10 (and_10_out, ~opcode[0], ~opcode[1], opcode[2], ~opcode[3], opcode[4]);  // AND_Gate
  and and_11 (isCall, opcode[0], opcode[1], ~opcode[2], ~opcode[3], opcode[4]);  // AND_Gate
  and and_12 (and_12_out, ~opcode[0], ~opcode[1], ~opcode[2], ~opcode[3], ~opcode[4]);  // AND_Gate
  and and_13 (and_13_out, opcode[1], opcode[2], opcode[3], ~opcode[4]);  // AND_Gate
  and isSub (ALUsignals[2], opcode[0], ~opcode[1], ~opcode[2], ~opcode[3], ~opcode[4]);  // AND_Gate
  and isCmp (ALUsignals[0], opcode[0], ~opcode[1], opcode[2], ~opcode[3], ~opcode[4]);  // AND_Gate
  and isMul (ALUsignals[3], ~opcode[0], opcode[1], ~opcode[2], ~opcode[3], ~opcode[4]);  // AND_Gate
  and isDiv (ALUsignals[4], opcode[0], opcode[1], ~opcode[2], ~opcode[3], ~opcode[4]);  // AND_Gate
  and isMod (ALUsignals[5], ~opcode[0], ~opcode[1], opcode[2], ~opcode[3], ~opcode[4]);  // AND_Gate
  and isLsl (ALUsignals[7], ~opcode[0], opcode[1], ~opcode[2], opcode[3], ~opcode[4]);  // AND_Gate
  and isLsr (ALUsignals[8], opcode[0], opcode[1], ~opcode[2], opcode[3], ~opcode[4]);  // AND_Gate
  and isAsr (ALUsignals[9], ~opcode[0], ~opcode[1], opcode[2], opcode[3], ~opcode[4]);  // AND_Gate
  and isOr (ALUsignals[12], opcode[0], opcode[1], opcode[2], ~opcode[3], ~opcode[4]);  // AND_Gate
  and isAnd (ALUsignals[11], ~opcode[0], opcode[1], opcode[2], ~opcode[3], ~opcode[4]);  // AND_Gate
  and isNot (ALUsignals[10], ~opcode[0], ~opcode[1], ~opcode[2], opcode[3], ~opcode[4]);  // AND_Gate
  and isMov (ALUsignals[6], opcode[0], ~opcode[1], ~opcode[2], opcode[3], ~opcode[4]);  // AND_Gate
  or or_1 (isUbranch, and_9_out, and_10_out);
  or isAdd (ALUsignals[1], and_12_out, and_13_out);
  nor nor_1 (isWb, and_6_out, and_7_out, and_8_out);

  assign isImmediate = I_bit;

  // Notes on the sheet:
  //   op1
  //   op2
  //   op3
  //   op4
  //   op5
endmodule

module Register_File (
  input  Clock,
  input  Reset,
  input  [31:0] WriteD,
  input  [3:0] ReadA1,
  input  WriteE,
  input  [3:0] WriteA,
  input  [3:0] ReadA2,
  input  [3:0] DisplayA,
  output [31:0] ReadD1,
  output [31:0] ReadD2,
  output [31:0] DisplayD
);

  wire demultiplexer_1_out0, demultiplexer_1_out1, demultiplexer_1_out2, demultiplexer_1_out3,
       demultiplexer_1_out4, demultiplexer_1_out5, demultiplexer_1_out6, demultiplexer_1_out7,
       demultiplexer_1_out8, demultiplexer_1_out9, demultiplexer_1_out10, demultiplexer_1_out11,
       demultiplexer_1_out12, demultiplexer_1_out13, demultiplexer_1_out14, demultiplexer_1_out15,
       multiplexer_2_out, or_1_out, or_2_out;
  wire [31:0] multiplexer_1_out, r0_q, r1_q, r2_q, r3_q, r4_q, r5_q, r6_q, r7_q, r8_q, r9_q, r10_q, r11_q,
       r12_q, r13_q, r14_q, r15_q;

  Demultiplexer #(.select(4), .disabled(0), .enable("false")) demultiplexer_1 (
    .out0(demultiplexer_1_out0), .out1(demultiplexer_1_out1), .out2(demultiplexer_1_out2),
    .out3(demultiplexer_1_out3), .out4(demultiplexer_1_out4), .out5(demultiplexer_1_out5),
    .out6(demultiplexer_1_out6), .out7(demultiplexer_1_out7), .out8(demultiplexer_1_out8),
    .out9(demultiplexer_1_out9), .out10(demultiplexer_1_out10), .out11(demultiplexer_1_out11),
    .out12(demultiplexer_1_out12), .out13(demultiplexer_1_out13), .out14(demultiplexer_1_out14),
    .out15(demultiplexer_1_out15), .in(WriteE), .sel(WriteA));
  Multiplexer #(.width(32), .enable("false")) multiplexer_1 (
    .in0(WriteD), .in1(32'h3fffffc), .out(multiplexer_1_out), .sel(Reset));
  or or_1 (or_1_out, demultiplexer_1_out14, Reset);
  Multiplexer #(.enable("false")) multiplexer_2 (.in0(or_2_out), .out(multiplexer_2_out), .sel(1'b0));  // open: in1
  or or_2 (or_2_out, Clock, Reset);
  Register #(.width(32)) r0 (.D(WriteD), .en(demultiplexer_1_out0), .Q(r0_q), .clk(Clock), .clr(Reset));
  Register #(.width(32)) r1 (.D(WriteD), .en(demultiplexer_1_out1), .Q(r1_q), .clk(Clock), .clr(Reset));
  Register #(.width(32)) r2 (.D(WriteD), .en(demultiplexer_1_out2), .Q(r2_q), .clk(Clock), .clr(Reset));
  Register #(.width(32)) r3 (.D(WriteD), .en(demultiplexer_1_out3), .Q(r3_q), .clk(Clock), .clr(Reset));
  Register #(.width(32)) r4 (.D(WriteD), .en(demultiplexer_1_out4), .Q(r4_q), .clk(Clock), .clr(Reset));
  Register #(.width(32)) r5 (.D(WriteD), .en(demultiplexer_1_out5), .Q(r5_q), .clk(Clock), .clr(Reset));
  Register #(.width(32)) r6 (.D(WriteD), .en(demultiplexer_1_out6), .Q(r6_q), .clk(Clock), .clr(Reset));
  Register #(.width(32)) r7 (.D(WriteD), .en(demultiplexer_1_out7), .Q(r7_q), .clk(Clock), .clr(Reset));
  Register #(.width(32)) r8 (.D(WriteD), .en(demultiplexer_1_out8), .Q(r8_q), .clk(Clock), .clr(Reset));
  Register #(.width(32)) r9 (.D(WriteD), .en(demultiplexer_1_out9), .Q(r9_q), .clk(Clock), .clr(Reset));
  Register #(.width(32)) r10 (.D(WriteD), .en(demultiplexer_1_out10), .Q(r10_q), .clk(Clock), .clr(Reset));
  Register #(.width(32)) r11 (.D(WriteD), .en(demultiplexer_1_out11), .Q(r11_q), .clk(Clock), .clr(Reset));
  Register #(.width(32)) r12 (.D(WriteD), .en(demultiplexer_1_out12), .Q(r12_q), .clk(Clock), .clr(Reset));
  Register #(.width(32)) r13 (.D(WriteD), .en(demultiplexer_1_out13), .Q(r13_q), .clk(Clock), .clr(Reset));
  Register #(.width(32)) r14 (.D(multiplexer_1_out), .en(or_1_out), .Q(r14_q), .clk(multiplexer_2_out));  // open: clr
  Register #(.width(32)) r15 (.D(WriteD), .en(demultiplexer_1_out15), .Q(r15_q), .clk(Clock), .clr(Reset));
  Multiplexer #(.select(4), .width(32), .disabled(0), .enable("false")) multiplexer_3 (
    .in0(r0_q), .in1(r1_q), .in2(r2_q), .in3(r3_q), .in4(r4_q), .in5(r5_q), .in6(r6_q), .in7(r7_q),
    .in8(r8_q), .in9(r9_q), .in10(r10_q), .in11(r11_q), .in12(r12_q), .in13(r13_q), .in14(r14_q),
    .in15(r15_q), .out(ReadD1), .sel(ReadA1));
  Multiplexer #(.select(4), .width(32), .disabled(0), .enable("false")) multiplexer_4 (
    .in0(r0_q), .in1(r1_q), .in2(r2_q), .in3(r3_q), .in4(r4_q), .in5(r5_q), .in6(r6_q), .in7(r7_q),
    .in8(r8_q), .in9(r9_q), .in10(r10_q), .in11(r11_q), .in12(r12_q), .in13(r13_q), .in14(r14_q),
    .in15(r15_q), .out(ReadD2), .sel(ReadA2));
  Multiplexer #(.select(4), .width(32), .disabled(0), .enable("false")) multiplexer_5 (
    .in0(r0_q), .in1(r1_q), .in2(r2_q), .in3(r3_q), .in4(r4_q), .in5(r5_q), .in6(r6_q), .in7(r7_q),
    .in8(r8_q), .in9(r9_q), .in10(r10_q), .in11(r11_q), .in12(r12_q), .in13(r13_q), .in14(r14_q),
    .in15(r15_q), .out(DisplayD), .sel(DisplayA));
endmodule

module ALU (
  input  [31:0] A,
  input  [31:0] B,
  input  [12:0] ALUsignals,
  output [31:0] aluResult,
  output is,
  output is_2
);

  wire [31:0] adder_1_out, and_1_out, divider_1_out, divider_1_rem, multiplier_1_out, not_1_out, or_1_out,
       shifter_1_out, shifter_2_out, shifter_3_out, subtractor_1_out;

  Adder #(.width(32)) adder_1 (.a(A), .b(B), .out(adder_1_out));  // open: cin, cout
  Subtractor #(.width(32)) subtractor_1 (.a(A), .b(B), .out(subtractor_1_out));  // open: bin, bout
  Multiplier #(.width(32)) multiplier_1 (.a(A), .b(B), .out(multiplier_1_out));  // open: cin, cout
  Divider #(.width(32)) divider_1 (.a(A), .b(B), .out(divider_1_out), .rem(divider_1_rem));  // open: upper
  Comparator #(.width(32)) comparator_1 (.a(A), .b(B), .gt(is), .eq(is_2));  // open: lt
  Shifter #(.width(32)) shifter_1 (.in(A), .\dist (B[4:0]), .out(shifter_1_out));
  Shifter #(.width(32), .shift("lr")) shifter_2 (.in(A), .\dist (B[4:0]), .out(shifter_2_out));
  Shifter #(.width(32), .shift("ar")) shifter_3 (.in(A), .\dist (B[4:0]), .out(shifter_3_out));
  assign not_1_out = ~B;  // NOT_Gate not_1, 32 bits wide
  assign and_1_out = A & B;  // AND_Gate and_1, 32 bits wide
  assign or_1_out = A | B;  // OR_Gate or_1, 32 bits wide
  assign aluResult = ALUsignals[1] ? adder_1_out : 32'bz;  // Controlled_Buffer controlled_buffer_1
  assign aluResult = ALUsignals[2] ? subtractor_1_out : 32'bz;  // Controlled_Buffer controlled_buffer_2
  assign aluResult = ALUsignals[3] ? multiplier_1_out : 32'bz;  // Controlled_Buffer controlled_buffer_3
  assign aluResult = ALUsignals[4] ? divider_1_out : 32'bz;  // Controlled_Buffer controlled_buffer_4
  assign aluResult = ALUsignals[5] ? divider_1_rem : 32'bz;  // Controlled_Buffer controlled_buffer_5
  assign aluResult = ALUsignals[6] ? B : 32'bz;  // Controlled_Buffer controlled_buffer_6
  assign aluResult = ALUsignals[7] ? shifter_1_out : 32'bz;  // Controlled_Buffer controlled_buffer_7
  assign aluResult = ALUsignals[8] ? shifter_2_out : 32'bz;  // Controlled_Buffer controlled_buffer_8
  assign aluResult = ALUsignals[9] ? shifter_3_out : 32'bz;  // Controlled_Buffer controlled_buffer_9
  assign aluResult = ALUsignals[10] ? not_1_out : 32'bz;  // Controlled_Buffer controlled_buffer_10
  assign aluResult = ALUsignals[11] ? and_1_out : 32'bz;  // Controlled_Buffer controlled_buffer_11
  assign aluResult = ALUsignals[12] ? or_1_out : 32'bz;  // Controlled_Buffer controlled_buffer_12

  // Notes on the sheet:
  //   add
  //   sub
  //   mul
  //   div
  //   cmp
  //   lsr
  //   mod
  //   lsl
  //   asr
endmodule

module Flags (
  input  isCmp,
  input  is,
  input  is_2,
  output flags_GT,
  output flags_E
);

  D_Flip_Flop #(.trigger("high")) d_ff_1 (.clk(isCmp), .D(is), .Q(flags_GT));  // open: Qn, preset, en, reset
  D_Flip_Flop #(.trigger("high")) d_ff_2 (.clk(isCmp), .D(is_2), .Q(flags_E));  // open: Qn, preset, en, reset
endmodule

module Branch_Unit (
  input  isUBranch,
  input  isBeq,
  input  flags_E,
  input  isBgt,
  input  flags_GT,
  output isBranchTaken
);

  wire and_1_out, and_2_out;

  and and_1 (and_1_out, isBeq, flags_E);
  and and_2 (and_2_out, isBgt, flags_GT);
  or or_1 (isBranchTaken, isUBranch, and_1_out, and_2_out);
endmodule

module Memory_Unit (
  input  [31:0] MAR,
  input  isLd,
  input  [31:0] MDR,
  input  isSt,
  input  Clock,
  input  Reset,
  output [31:0] ldResult
);

  RAM #(.addrWidth(24), .dataWidth(32), .bus("separate")) ram_1 (
    .addr(MAR[25:2]), .din(MDR), .data(ldResult), .str(isSt), .clk(Clock), .ld(isLd), .clr(Reset));  // open: sel
endmodule

module Calculate_Immediate (
  input  [17:0] imm,
  output [31:0] immx
);

  wire [31:0] bit_extender_1_out, bit_extender_2_out, shifter_1_out;

  assign bit_extender_1_out = {{16{1'b0}}, imm[15:0]};  // Bit_Extender bit_extender_1
  assign bit_extender_2_out = {{16{imm[15]}}, imm[15:0]};  // Bit_Extender bit_extender_2
  Shifter #(.width(32)) shifter_1 (.in(bit_extender_1_out), .\dist (5'b10000), .out(shifter_1_out));
  Multiplexer #(.select(2), .width(32), .enable("false")) multiplexer_1 (
    .in0(bit_extender_2_out), .in1(bit_extender_1_out), .in2(shifter_1_out), .out(immx), .sel(imm[17:16]));  // open: in3

  // Notes on the sheet:
  //   modifier bits
  //   high
  //   default
  //   unsigned
endmodule
